# Fritzing sketch Untitled Sketch 2 (saved by Fritzing 0.8.7b)
breadboards: 1

parts:
  Part1 = Arduino Leonardo (Rev3b)
  LCD1 = LCD screen
  U1 = POT [package=pot_mammoth]
  U2 = 74HC595 [package="DIP16 [THT]"]  # not connected
  R1 = Resistor [tolerance=±5% resistance=220 package=THT]
  T1 = LM35 Temperature Sensor [package="TO92 [THT]"]
  LED1 = LED - 5mm [color="Red (633nm)" package="5 mm [THT]"]
  R2 = Resistor [tolerance=±5% resistance=220 package=THT]

nets:
  5V: Part1.5V, Part1.D8/A8, LCD1.VDD, U1.E, R1.Pin_0
  N1: Part1.D9_PWM/A9, R2.Pin_1
  GND: Part1.GND, LCD1.VSS, U1.S, T1.+Vs, T1.GND, LED1.cathode
  N2: LCD1.V0, U1.A
  N3: R1.Pin_1, T1.Vout
  N4: LED1.anode, R2.Pin_0
